# Fritzing sketch setup (saved by Fritzing 0.9.3b)
breadboards: 1

parts:
  WeMos_D1_Mini2 = WeMos D1 Mini  # not connected
  DFRobot_DFPlayer_Mini1 = DFRobot DFPlayer Mini [part_number=DFR0299]
  SP1 = SPEAKER [package=pcb_mount_speaker]  # not connected
  R1 = Resistor [tolerance=±5% resistance=1k package=THT]
  Part1 = PowerBoost 500 Charger
  U2 = LIPO-1000mAh [package=lipo-1000]
  R2 = Resistor [tolerance=±5% resistance=1M package=THT]
  R3 = Textile Analog Pressure Sensor [part_number=PW073]

nets:
  N1: DFRobot_DFPlayer_Mini1.RX, R1.Pin_1
  N2: Part1.GND_BAT_IN, U2.-
  N3: Part1.VBAT_IN, U2.+
  N4: R2.Pin_0, R3.pin_1

notes:
  [Ultrasound]
  VCC>5V------
  GND>GND--
  SIG>D1------
  NC----x
  [MP3-TF-16P]
  ---- 5V<VCC
  ---- D3< RX
  ---- D2< TX
  ----
  ---- SPK_1
  ---- Gnd
  ---- SPK_2
  [VMA408]
  O --- -Rin
  O --- Gnd
  O --- Lin
  O --- Sw
  O --- 5V
  O --- Gnd
  O --- L+
  O --- L-
  O --- R-
  O --- R+
  ==== >===Powerboost 1000C ===>
  ==== >==== to WEMOS =========>
  charger
  input ->
  1KΩ
  1MΩ @ D8,D5
  alligator clip
  ALUMINIUM
